# Fritzing sketch CAPSICUM (saved by Fritzing 0.9.3b)
circuit board: 8.36311cm x 6.08467cm
breadboards: 1

parts:
  Power_plug1 = Power plug
  7805 = Voltage Regulator - 5V [package="TO220 [THT]"]
  1μF = Electrolytic Capacitor [capacitance=1µF package="100 mil [THT, electrolytic]"]
  1μF_2 = Electrolytic Capacitor [capacitance=1µF package="100 mil [THT, electrolytic]"]
  1N4007 = Rectifier Diode [part_number=1N4001 package="300 mil [THT]"]
  220Ω = Resistor [tolerance=±5% resistance=220 package=THT]
  220Ω_2 = Resistor [tolerance=±5% resistance=220 package=THT]
  10KΩ = Resistor [tolerance=±5% resistance=10k package=THT]
  MIDI_OUT = DIN-5 jack (MIDI) [package=THT]
  22pF = Ceramic Capacitor [capacitance=10pF package="100 mil [THT, multilayer]"]
  100nF = Ceramic Capacitor [capacitance=100nF package="200 mil [THT, multilayer]"]
  J14 = female pin header, 6 pins [form="♀ (female)"]
  MIDI_IN = DIN-5 jack (MIDI) [package=THT]
  16Mhz = Crystal [frequency="16 Mhz" package=THT]
  22pF_2 = Ceramic Capacitor [capacitance=100nF package="100 mil [THT, multilayer]"]
  220Ω_3 = Resistor [tolerance=±5% resistance=220 package=THT]
  J15 = female pin header, 20 pins [form="♀ (female)"]
  J16 = female pin header, 4 pins [form="♀ (female)"]
  220Ω_4 = Resistor [tolerance=±5% resistance=220 package=THT]
  1N4148 = Schottky Diode [part_number=1N4148 package="300 mil [THT]"]
  ATMEGA328P-PU = atmega328 [package=dip]
  MIDI/PGM = SWITCH-DPDT [package=eg2211]
  6N138 = IC, DIP package, 8 pins [chip_label=IC]

nets:
  GND: Power_plug1.GND, 7805.GND, 1μF.-, 1μF_2.-, MIDI_OUT.2, MIDI_OUT.GND, 22pF.1, J14.pin6, MIDI_IN.GND, 22pF_2.0, J15.pin20, J16.pin1, ATMEGA328P-PU.GND, 6N138.pin5
  N1: Power_plug1.VCC, 1N4007.anode
  N2: 7805.input_voltage, 1μF_2.+, 1N4007.cathode, J16.pin2
  N3: 7805.output_voltage, 1μF.+, 220Ω.Pin_1, 10KΩ.Pin_1, J15.pin19, J16.pin3, 220Ω_4.Pin_0, ATMEGA328P-PU.VCC, ATMEGA328P-PU.AVCC, ATMEGA328P-PU.AREF, 6N138.pin8
  N4: 220Ω.Pin_0, MIDI_OUT.4
  N5: 220Ω_2.Pin_0, MIDI_IN.4
  N6: 220Ω_2.Pin_1, 1N4148.cathode, 6N138.pin2
  N7: 10KΩ.Pin_0, 100nF.0, J16.pin4, ATMEGA328P-PU.RESET
  N8: MIDI_OUT.5, 220Ω_3.Pin_0
  N9: 22pF.0, 16Mhz.pin_1, ATMEGA328P-PU.XLAT2
  N10: 100nF.1, J14.pin1
  N11: J14.pin2, 220Ω_3.Pin_1, ATMEGA328P-PU.D1_(TX)
  N12: J14.pin3, ATMEGA328P-PU.D0_(RX), MIDI/PGM.2, MIDI/PGM.5
  N13: MIDI_IN.5, 1N4148.anode, 6N138.pin3
  N14: 16Mhz.pin_0, 22pF_2.1, ATMEGA328P-PU.XLAT1
  N15: J15.pin1, ATMEGA328P-PU.A5
  N16: J15.pin2, ATMEGA328P-PU.A4
  N17: J15.pin3, ATMEGA328P-PU.A3
  N18: J15.pin4, ATMEGA328P-PU.A2
  N19: J15.pin5, ATMEGA328P-PU.A1
  N20: J15.pin6, ATMEGA328P-PU.A0
  N21: J15.pin7, ATMEGA328P-PU.D13
  N22: J15.pin8, ATMEGA328P-PU.D12
  N23: J15.pin9, ATMEGA328P-PU.D11_(PWM)
  N24: J15.pin10, ATMEGA328P-PU.D10_(PWM)
  N25: J15.pin11, ATMEGA328P-PU.D9_(PWM)
  N26: J15.pin12, ATMEGA328P-PU.D8
  N27: J15.pin13, ATMEGA328P-PU.D7
  N28: J15.pin14, ATMEGA328P-PU.D6_(PWM)
  N29: J15.pin15, ATMEGA328P-PU.D5_(PWM)
  N30: J15.pin16, ATMEGA328P-PU.D4
  N31: J15.pin17, ATMEGA328P-PU.D3_(PWM)
  N32: J15.pin18, ATMEGA328P-PU.D2
  N33: 220Ω_4.Pin_1, MIDI/PGM.3, MIDI/PGM.6, 6N138.pin6
  N34: MIDI/PGM.1, MIDI/PGM.4

notes:
  GND
  5V
  D2
  A0
  D3
  D4
  D8
  D7
  D5
  D6
  A2
  A1
  D12
  D11
  D13
  D9
  D10
  A3
  A5
  A4
  RST
  Vin
  6N138
  Rst
  DTR
  TX
  RX
  +•)-
  9/12V
  MIDI IN/OUT/THRU TOOL
  7
