# Fritzing sketch CHIPOTLE (saved by Fritzing 0.9.3b)
circuit board: 11.0442cm x 7.94733cm
breadboards: 1

parts:
  J15 = female pin header, 20 pins [form="♀ (female)"]
  J17 = female pin header, 4 pins [form="♀ (female)"]
  R7 = Rotary Potentiometer (Small) [maximum_resistance=10kΩ package=THT]
  R8 = Rotary Potentiometer (Small) [maximum_resistance=10kΩ package=THT]
  R9 = Rotary Potentiometer (Small) [maximum_resistance=10kΩ package=THT]
  R10 = Rotary Potentiometer (Small) [maximum_resistance=10kΩ package=THT]
  R11 = Rotary Potentiometer (Small) [maximum_resistance=10kΩ package=THT]
  R12 = Rotary Potentiometer (Small) [maximum_resistance=10kΩ package=THT]
  JP1 = RCA [package=rca_lock]
  JP5 = RCA [package=rca_lock]
  JP6 = RCA [package=rca_lock]
  JP7 = RCA [package=rca_lock]
  JP8 = RCA [package=rca_lock]
  LED = LED - 5mm [color="Red (633nm)" package="5 mm [THT]"]
  R21 = Resistor [tolerance=±5% resistance=220 package=THT]
  S1 = Pushbutton [package="[THT]"]
  IRFZ44N = Basic FET N-Channel [package="TO220 [THT]"]
  IRFZ44N_2 = Basic FET N-Channel [package="TO220 [THT]"]
  IRFZ44N_3 = Basic FET N-Channel [package="TO220 [THT]"]
  D10 = Rectifier Diode [part_number=1N4001 package="300 mil [THT]"]
  D11 = Rectifier Diode [part_number=1N4001 package="300 mil [THT]"]
  D12 = Rectifier Diode [part_number=1N4001 package="300 mil [THT]"]
  R24 = Resistor [tolerance=±5% resistance=10k package=THT]
  R25 = Resistor [tolerance=±5% resistance=10k package=THT]
  R26 = Resistor [tolerance=±5% resistance=10k package=THT]
  IRFZ44N_4 = Basic FET N-Channel [package="TO220 [THT]"]
  D13 = Rectifier Diode [part_number=1N4001 package="300 mil [THT]"]
  R27 = Resistor [tolerance=±5% resistance=10k package=THT]
  IRFZ44N_5 = Basic FET N-Channel [package="TO220 [THT]"]
  D14 = Rectifier Diode [part_number=1N4001 package="300 mil [THT]"]
  R28 = Resistor [tolerance=±5% resistance=10k package=THT]
  JP9 = RCA [package=rca_lock]
  IRFZ44N_6 = Basic FET N-Channel [package="TO220 [THT]"]
  D15 = Rectifier Diode [part_number=1N4001 package="300 mil [THT]"]
  R29 = Resistor [tolerance=±5% resistance=10k package=THT]
  SW1 = SPDT Toggle Switch
  SW2 = SPDT Toggle Switch
  SW3 = SPDT Toggle Switch
  SW4 = SPDT Toggle Switch
  SW5 = SPDT Toggle Switch
  SW6 = SPDT Toggle Switch
  Power_plug2 = Power plug
  D17 = Rectifier Diode [part_number=1N4001 package="300 mil [THT]"]
  J23 = male pin header, 3 pins [form="♂ (male)"]
  LED_2 = LED - 3mm [color="Red (633nm)" package="3 mm [THT]"]
  R30 = Resistor [tolerance=±5% resistance=220 package=THT]
  R31 = Resistor [tolerance=±5% resistance=220 package=THT]
  LED_3 = LED - 3mm [color="Red (633nm)" package="3 mm [THT]"]
  R32 = Resistor [tolerance=±5% resistance=220 package=THT]
  LED_4 = LED - 3mm [color="Red (633nm)" package="3 mm [THT]"]
  R33 = Resistor [tolerance=±5% resistance=220 package=THT]
  LED_5 = LED - 3mm [color="Red (633nm)" package="3 mm [THT]"]
  R34 = Resistor [tolerance=±5% resistance=220 package=THT]
  LED_6 = LED - 3mm [color="Red (633nm)" package="3 mm [THT]"]
  R35 = Resistor [tolerance=±5% resistance=220 package=THT]
  LED_7 = LED - 3mm [color="Red (633nm)" package="3 mm [THT]"]

nets:
  N1: J15.pin1, R11.wiper
  N2: J15.pin2, R12.wiper
  N3: J15.pin3, R10.wiper
  N4: J15.pin4, R9.wiper
  N5: J15.pin5, R8.wiper
  N6: J15.pin6, R7.wiper
  N7: J15.pin9, SW1.3, LED_2.anode
  N8: J15.pin10, SW2.3, LED_3.anode
  N9: J15.pin11, SW3.3, LED_4.anode
  N10: J15.pin14, SW4.3, LED_5.anode
  N11: J15.pin15, SW5.3, LED_6.anode
  N12: J15.pin17, SW6.3, LED_7.anode
  N13: J15.pin19, R7.leg2, R8.leg2, R9.leg2, R10.leg2, R11.leg2, R12.leg2
  N14: J15.pin20, R7.leg1, R8.leg1, R9.leg1, R10.leg1, R11.leg1, R12.leg1
  N15: J17.pin1, IRFZ44N.source, IRFZ44N_2.source, IRFZ44N_3.source, R24.Pin_1, R25.Pin_1, R26.Pin_1, IRFZ44N_4.source, R27.Pin_1, IRFZ44N_5.source, R28.Pin_1, IRFZ44N_6.source, R29.Pin_1, R30.Pin_0, R31.Pin_0, R32.Pin_0, R33.Pin_0, R34.Pin_0, R35.Pin_0
  N16: J17.pin2, J23.pin3
  N17: J17.pin3, R21.Pin_0
  N18: J17.pin4, S1.Pin_3, S1.Pin_4
  N19: JP1.PIN, JP5.PIN, JP6.PIN, JP7.PIN, JP8.PIN, D10.cathode, D11.cathode, D12.cathode, D13.cathode, D14.cathode, JP9.PIN, D15.cathode, J23.pin2
  N20: JP1.SHELL, IRFZ44N_5.drain, D14.anode
  N21: JP5.SHELL, IRFZ44N_4.drain, D13.anode
  N22: JP6.SHELL, IRFZ44N_3.drain, D12.anode
  N23: JP7.SHELL, IRFZ44N_2.drain, D10.anode
  N24: JP8.SHELL, IRFZ44N.drain, D11.anode
  N25: LED.cathode, S1.Pin_1, S1.Pin_2, Power_plug2.GND
  N26: LED.anode, R21.Pin_1
  N27: IRFZ44N.gate, R24.Pin_0, SW5.2
  N28: IRFZ44N_2.gate, R25.Pin_0, SW4.2
  N29: IRFZ44N_3.gate, R26.Pin_0, SW3.2
  N30: IRFZ44N_4.gate, R27.Pin_0, SW1.2
  N31: IRFZ44N_5.gate, R28.Pin_0, SW2.2
  N32: JP9.SHELL, IRFZ44N_6.drain, D15.anode
  N33: IRFZ44N_6.gate, R29.Pin_0, SW6.2
  N34: Power_plug2.VCC, D17.anode
  N35: D17.cathode, J23.pin1
  N36: LED_2.cathode, R30.Pin_1
  N37: R31.Pin_1, LED_3.cathode
  N38: R32.Pin_1, LED_4.cathode
  N39: R33.Pin_1, LED_5.cathode
  N40: R34.Pin_1, LED_6.cathode
  N41: R35.Pin_1, LED_7.cathode

notes:
  A1
  A2
  A3
  A4
  A5
  A0
  Rst
  5V
  GND
  Vin
  D3
  D5
  D6
  D11
  D10
  D9
  Vup
  Vdwn
  D13
  D12
  D8
  D7
  D4
  D2
  HIGH POWER
  CONTROLLER
  M I D I

custom parts:
  SPDT Toggle Switch: SPDT Toggle Switch. On-On
