# Fritzing sketch panka (saved by Fritzing 0.9.3b)
circuit board: 15cm x 6.08467cm
breadboards: 1

parts:
  J16 = female pin header, 20 pins [form="♀ (female)"]
  Pad11 = Pad [width=8.5999999999999996 height=34 connect=center]
  Pad10 = Pad [width=8.5999999999999996 height=40 connect=center]
  Pad12 = Pad [width=8.5999999999999996 height=40 connect=center]
  Pad14 = Pad [width=8.5999999999999996 height=40 connect=center]
  Pad13 = Pad [width=8.5999999999999996 height=40 connect=center]
  Pad16 = Pad [width=8.5999999999999996 height=40 connect=center]
  Pad9 = Pad [width=8.5999999999999996 height=40 connect=center]
  Pad15 = Pad [width=8.5999999999999996 height=40 connect=center]
  Pad6 = Pad [width=8.5999999999999996 height=40 connect=center]
  Pad7 = Pad [width=8.5999999999999996 height=40 connect=center]
  Pad5 = Pad [width=8.5999999999999996 height=40 connect=center]
  Pad8 = Pad [width=8.5999999999999996 height=40 connect=center]
  Pad4 = Pad [width=8.5999999999999996 height=40 connect=center]
  Pad3 = Pad [width=8.5999999999999996 height=40 connect=center]
  Pad2 = Pad [width=8.5999999999999996 height=40 connect=center]
  Pad1 = Pad [width=8.5999999999999996 height=34 connect=center]
  R1 = Resistor [tolerance=±5% resistance=220 package="1206 [SMD]"]
  RGB_SMD_LED1 = SMD RGB LED (WS2812) [package=5050]
  J17 = female pin header, 1 pin [form="♀ (female)"]
  Pad231 = Pad [width=1.3400000000000001 height=2.032 connect=center]
  Pad232 = Pad [width=1.3400000000000001 height=2.032 connect=center]
  Pad233 = Pad [width=1.3400000000000001 height=2.032 connect=center]
  Pad234 = Pad [width=1.3400000000000001 height=2.032 connect=center]
  Pad235 = Pad [width=1.3400000000000001 height=2.032 connect=center]
  Pad236 = Pad [width=1.3400000000000001 height=2.032 connect=center]
  C1 = Ceramic Capacitor [capacitance=100nF package="1206 [SMD, multilayer]"]
  S1 = Pushbutton [package="[THT]"]
  Pad237 = Pad [width=3.5526227407407434 height=11.045801481481481 connect=center]
  Pad238 = Pad [width=3.8348355555555558 height=10.340255333333333 connect=center]
  LED1 = smd LED [color="Red (633nm)" package="1206 [SMD]"]
  R2 = Resistor [tolerance=±5% resistance=220 package="1206 [SMD]"]

nets:
  N1: J16.pin1, Pad11.pad, Pad238.pad
  N2: J16.pin2, Pad10.pad
  N3: J16.pin3, Pad12.pad
  N4: J16.pin4, Pad14.pad
  N5: J16.pin5, Pad13.pad
  N6: J16.pin6, Pad16.pad
  N7: J16.pin7, Pad9.pad
  N8: J16.pin8, Pad15.pad
  N9: J16.pin9, Pad6.pad
  N10: J16.pin10, Pad7.pad
  N11: J16.pin11, Pad5.pad
  N12: J16.pin12, Pad8.pad
  N13: J16.pin13, Pad4.pad
  N14: J16.pin14, Pad3.pad
  N15: J16.pin15, Pad2.pad
  N16: J16.pin16, Pad1.pad, Pad237.pad
  N17: J16.pin17, R1.Pin_1
  N18: J16.pin18, S1.Pin_3, S1.Pin_4
  VCC: J16.pin19, RGB_SMD_LED1.VCC, RGB_SMD_LED1.VDD, Pad231.pad, Pad234.pad, C1.0, LED1.anode
  N19: J16.pin20, RGB_SMD_LED1.VSS, J17.pin1, Pad236.pad, C1.1, S1.Pin_1, S1.Pin_2, R2.Pin_0
  N20: R1.Pin_0, RGB_SMD_LED1.DIn, Pad232.pad
  N21: RGB_SMD_LED1.DOut, Pad233.pad
  N22: RGB_SMD_LED1.NC, Pad235.pad
  N23: LED1.cathode, R2.Pin_1
