# Fritzing sketch PEPERONCINO (saved by Fritzing 0.9.3b)
circuit board: 6.26055cm x 5.92944cm
breadboards: 1

parts:
  220Ω = Resistor [tolerance=±5% resistance=220 package=THT]
  220Ω_2 = Resistor [tolerance=±5% resistance=220 package=THT]
  OUT = DIN-5 jack (MIDI) [package=THT]
  IN = DIN-5 jack (MIDI) [package=THT]
  220Ω_3 = Resistor [tolerance=±5% resistance=220 package=THT]
  220Ω_4 = Resistor [tolerance=±5% resistance=220 package=THT]
  1N4148 = Schottky Diode [part_number=1N4148 package="300 mil [THT]"]
  6N138 = IC, DIP package, 8 pins [chip_label=IC]
  MIDI/PGM = SWITCH-DPDT [package=eg2211]
  ioref = Arduino Uno (Rev3)
  220Ω_5 = Resistor [tolerance=±5% resistance=220 package=THT]
  J28 = female pin header, 6 pins [form="♀ (female)"]
  J29 = female pin header, 10 pins [form="♀ (female)"]
  J30 = female pin header, 8 pins [form="♀ (female)"]
  dip1 = female pin header, 8 pins [form="♀ (female)"]
  LED1 = LED - 3mm [color="Red (633nm)" package="3 mm [THT]"]
  RST = Pushbutton [package="[THT]"]
  LED2 = LED - 3mm [color="Red (633nm)" package="3 mm [THT]"]
  J34 = female pin header, 10 pins [form="♀ (female)"]  # not connected
  J33 = female pin header, 10 pins [form="♀ (female)"]  # not connected
  J35 = female pin header, 10 pins [form="♀ (female)"]  # not connected
  J36 = female pin header, 10 pins [form="♀ (female)"]  # not connected
  J31 = female pin header, 10 pins [form="♀ (female)"]  # not connected
  J32 = female pin header, 10 pins [form="♀ (female)"]  # not connected
  GND = female pin header, 6 pins [form="♀ (female)"]
  5V = female pin header, 6 pins [form="♀ (female)"]
  J39 = female pin header, 8 pins [form="♀ (female)"]  # not connected
  J41 = female pin header, 8 pins [form="♀ (female)"]  # not connected
  J40 = female pin header, 8 pins [form="♀ (female)"]  # not connected
  J42 = female pin header, 8 pins [form="♀ (female)"]  # not connected
  J44 = female pin header, 10 pins [form="♀ (female)"]
  J43 = female pin header, 10 pins [form="♀ (female)"]
  J37 = female pin header, 10 pins [form="♀ (female)"]
  J45 = female pin header, 1 pin [form="♀ (female)"]
  J46 = female pin header, 1 pin [form="♀ (female)"]
  J47 = female pin header, 1 pin [form="♀ (female)"]
  J48 = female pin header, 1 pin [form="♀ (female)"]
  J49 = female pin header, 1 pin [form="♀ (female)"]
  J50 = female pin header, 1 pin [form="♀ (female)"]

nets:
  N1: 220Ω.Pin_0, OUT.4
  N2: 220Ω.Pin_1, 220Ω_4.Pin_0, 6N138.pin8, ioref.5V, dip1.pin4, LED1.anode, 5V.pin1, 5V.pin2, 5V.pin3, 5V.pin4, 5V.pin5, 5V.pin6, J43.pin1, J43.pin2, J43.pin3, J43.pin4, J43.pin5, J43.pin6, J43.pin7, J43.pin8, J43.pin9, J43.pin10
  N3: 220Ω_2.Pin_0, IN.4
  N4: 220Ω_2.Pin_1, 1N4148.cathode, 6N138.pin2
  N5: OUT.5, 220Ω_3.Pin_0
  N6: OUT.2, IN.2, 6N138.pin5, ioref.GND, 220Ω_5.Pin_0, J29.pin7, dip1.pin2, dip1.pin3, RST.Pin_3, RST.Pin_4, LED2.cathode, GND.pin1, GND.pin2, GND.pin3, GND.pin4, GND.pin5, GND.pin6, J44.pin1
  N7: IN.5, 1N4148.anode, 6N138.pin3
  N8: 220Ω_3.Pin_1, ioref.D1/TX, J30.pin2
  N9: 220Ω_4.Pin_1, 6N138.pin6, MIDI/PGM.3, MIDI/PGM.6
  N10: MIDI/PGM.2, MIDI/PGM.5, ioref.D0/RX, J30.pin1
  N11: MIDI/PGM.1, MIDI/PGM.4
  N12: ioref.A0, J28.pin6, J45.pin1
  N13: ioref.A1, J28.pin5, J46.pin1
  N14: ioref.A2, J28.pin4, J47.pin1
  N15: ioref.A3, J28.pin3, J48.pin1
  N16: ioref.A4/SDA, J28.pin2, J29.pin9, J49.pin1
  N17: ioref.A5/SCL, J28.pin1, J29.pin10, J50.pin1
  N18: ioref.D8, J29.pin1
  N19: ioref.D9_PWM, J29.pin2
  N20: ioref.D10_PWM/SS, J29.pin3
  N21: ioref.D11_PWM/MOSI, J29.pin4
  N22: ioref.D12/MISO, J29.pin5
  N23: ioref.D13/SCK, J29.pin6, LED2.anode
  N24: ioref.AREF, J29.pin8
  N25: ioref.D2, J30.pin3
  N26: ioref.D3_PWM, J30.pin4
  N27: ioref.D4, J30.pin5
  N28: ioref.D5_PWM, J30.pin6
  N29: ioref.D6_PWM, J30.pin7
  N30: ioref.D7, J30.pin8
  N31: ioref.ioref, dip1.pin7
  N32: ioref.RESET, dip1.pin6, RST.Pin_1, RST.Pin_2
  N33: ioref.3V3, dip1.pin5
  N34: ioref.VIN, dip1.pin1, J37.pin1, J37.pin2, J37.pin3, J37.pin4, J37.pin5, J37.pin6, J37.pin7, J37.pin8, J37.pin9, J37.pin10
  N35: ioref.N/C, dip1.pin8
  N36: 220Ω_5.Pin_1, LED1.cathode

notes:
  GND
  5V
  D2
  A0
  D3
  D4
  D8
  D7
  D5
  D6
  A2
  A1
  D12
  D11
  D13
  D9
  D10
  A3
  A5
  A4
  RST
  Vin
  6N138
  7
  3.3
  IOREF
  RX
  D5~
  D3~
  TX
  D6~
  AREF
  D11~
  D10~
  D9~
  SDA
  SCL
  IN
  MIDI
  shield
  Ain
