# Fritzing sketch ROCOTO (saved by Fritzing 0.9.3b)
circuit board: 18.086cm x 8.1052cm
breadboards: 1

parts:
  J15 = female pin header, 20 pins [form="♀ (female)"]
  J17 = female pin header, 4 pins [form="♀ (female)"]
  relay_5 = DIP - 8 pins [chip_label=IC package="DIP (Dual Inline) [THT]"]
  NO_/_NC = SPDT Toggle Switch
  R7 = Rotary Potentiometer (Small) [maximum_resistance=100kΩ package=THT]
  R8 = Rotary Potentiometer (Small) [maximum_resistance=100kΩ package=THT]
  R9 = Rotary Potentiometer (Small) [maximum_resistance=100kΩ package=THT]
  R10 = Rotary Potentiometer (Small) [maximum_resistance=100kΩ package=THT]
  R11 = Rotary Potentiometer (Small) [maximum_resistance=100kΩ package=THT]
  R12 = Rotary Potentiometer (Small) [maximum_resistance=100kΩ package=THT]
  E = RCA [package=rca_lock]
  relay_6 = DIP - 8 pins [chip_label=IC package="DIP (Dual Inline) [THT]"]
  NO_/_NC_2 = SPDT Toggle Switch
  F = RCA [package=rca_lock]
  relay_4 = DIP - 8 pins [chip_label=IC package="DIP (Dual Inline) [THT]"]
  NO_/_NC_3 = SPDT Toggle Switch
  D = RCA [package=rca_lock]
  relay_3 = DIP - 8 pins [chip_label=IC package="DIP (Dual Inline) [THT]"]
  NO_/_NC_4 = SPDT Toggle Switch
  C = RCA [package=rca_lock]
  B = RCA [package=rca_lock]
  A = RCA [package=rca_lock]
  relay_2 = DIP - 8 pins [chip_label=IC package="DIP (Dual Inline) [THT]"]
  NO_/_NC_5 = SPDT Toggle Switch
  NO_/_NC_6 = SPDT Toggle Switch
  R21 = Resistor [tolerance=±5% resistance=220 package=THT]
  RST = Pushbutton [package="[THT]"]
  LED15 = LED - 3mm [color="Red (633nm)" package="3 mm [THT]"]
  R22 = Resistor [tolerance=±5% resistance=220 package=THT]
  LED16 = LED - 3mm [color="Red (633nm)" package="3 mm [THT]"]
  LED17 = LED - 3mm [color="Red (633nm)" package="3 mm [THT]"]
  R23 = Resistor [tolerance=±5% resistance=220 package=THT]
  LED18 = LED - 3mm [color="Red (633nm)" package="3 mm [THT]"]
  R24 = Resistor [tolerance=±5% resistance=220 package=THT]
  LED19 = LED - 3mm [color="Red (633nm)" package="3 mm [THT]"]
  R25 = Resistor [tolerance=±5% resistance=220 package=THT]
  LED20 = LED - 3mm [color="Red (633nm)" package="3 mm [THT]"]
  R26 = Resistor [tolerance=±5% resistance=220 package=THT]
  LED21 = LED - 3mm [color="Red (633nm)" package="3 mm [THT]"]
  R27 = Resistor [tolerance=±5% resistance=220 package=THT]
  S6 = Toggle Switch [package=THT]
  S7 = Toggle Switch [package=THT]
  S8 = Toggle Switch [package=THT]
  S9 = Toggle Switch [package=THT]
  S10 = Toggle Switch [package=THT]
  S11 = Toggle Switch [package=THT]
  R28 = Resistor [tolerance=±5% resistance=220 package=THT]
  LED22 = LED - 3mm [color="Red (633nm)" package="3 mm [THT]"]
  LED23 = LED - 3mm [color="Red (633nm)" package="3 mm [THT]"]
  R29 = Resistor [tolerance=±5% resistance=220 package=THT]
  LED24 = LED - 3mm [color="Red (633nm)" package="3 mm [THT]"]
  R30 = Resistor [tolerance=±5% resistance=220 package=THT]
  LED25 = LED - 3mm [color="Red (633nm)" package="3 mm [THT]"]
  R31 = Resistor [tolerance=±5% resistance=220 package=THT]
  S12 = Toggle Switch [package=THT]
  S13 = Toggle Switch [package=THT]
  LED26 = LED - 3mm [color="Red (633nm)" package="3 mm [THT]"]
  R32 = Resistor [tolerance=±5% resistance=220 package=THT]
  S14 = Toggle Switch [package=THT]
  S15 = Toggle Switch [package=THT]
  LED27 = LED - 3mm [color="Red (633nm)" package="3 mm [THT]"]
  R33 = Resistor [tolerance=±5% resistance=220 package=THT]
  S16 = Toggle Switch [package=THT]
  S17 = Toggle Switch [package=THT]
  ULN2003/4 = ULN2003A [package="SO16 [SMD]"]
  relay_1 = DIP - 8 pins [chip_label=IC package="DIP (Dual Inline) [THT]"]

nets:
  N1: J15.pin1, R11.wiper
  N2: J15.pin2, R12.wiper
  N3: J15.pin3, R10.wiper
  N4: J15.pin4, R9.wiper
  N5: J15.pin5, R8.wiper
  N6: J15.pin6, R7.wiper
  N7: J15.pin7, S16.L2
  N8: J15.pin8, S14.L2
  N9: J15.pin9, S12.L2
  N10: J15.pin11, S8.L2
  N11: J15.pin12, S10.L2
  N12: J15.pin13, ULN2003/4.In_2
  N13: J15.pin14, ULN2003/4.In_3
  N14: J15.pin15, ULN2003/4.In_4
  N15: J15.pin16, ULN2003/4.In_5
  N16: J15.pin17, ULN2003/4.In_6
  N17: J15.pin18, ULN2003/4.In_7
  N18: J15.pin20, R7.leg1, R8.leg1, R9.leg1, R10.leg1, R11.leg1, R12.leg1, S6.COM, S7.COM, S8.COM, S9.COM, S10.COM, S11.COM, S12.COM, S13.COM, S14.COM, S15.COM, S16.COM, S17.COM, ULN2003/4.0V
  N19: J17.pin1, RST.Pin_1, RST.Pin_2, LED15.cathode
  N20: J17.pin3, relay_5.pin4, R7.leg2, R8.leg2, R9.leg2, R10.leg2, R11.leg2, R12.leg2, relay_6.pin4, relay_4.pin4, relay_3.pin4, relay_2.pin4, R21.Pin_0, LED16.anode, LED17.anode, LED18.anode, LED19.anode, LED20.anode, LED21.anode, LED22.anode, LED23.anode, LED24.anode, LED25.anode, LED26.anode, LED27.anode, ULN2003/4.COM_-_Common, relay_1.pin4
  N21: J17.pin4, RST.Pin_3, RST.Pin_4
  N22: relay_5.pin1, NO_/_NC.1
  N23: relay_5.pin2, NO_/_NC.3
  N24: relay_5.pin3, E.SHELL
  N25: relay_5.pin5, R24.Pin_1, ULN2003/4.Out_3
  N26: NO_/_NC.2, E.PIN, E.SWITCH
  N27: relay_6.pin1, NO_/_NC_2.1
  N28: relay_6.pin2, NO_/_NC_2.3
  N29: relay_6.pin3, F.SHELL
  N30: relay_6.pin5, R25.Pin_1, ULN2003/4.Out_2
  N31: NO_/_NC_2.2, F.PIN, F.SWITCH
  N32: relay_4.pin1, NO_/_NC_3.1
  N33: relay_4.pin2, NO_/_NC_3.3
  N34: relay_4.pin3, D.SHELL
  N35: relay_4.pin5, R23.Pin_1, ULN2003/4.Out_4
  N36: NO_/_NC_3.2, D.PIN, D.SWITCH
  N37: relay_3.pin1, NO_/_NC_4.1
  N38: relay_3.pin2, NO_/_NC_4.3
  N39: relay_3.pin3, C.SHELL
  N40: relay_3.pin5, R22.Pin_1, ULN2003/4.Out_5
  N41: NO_/_NC_4.2, C.PIN, C.SWITCH
  N42: B.PIN, B.SWITCH, NO_/_NC_5.2
  N43: B.SHELL, relay_2.pin3
  N44: A.PIN, A.SWITCH, NO_/_NC_6.2
  N45: A.SHELL, relay_1.pin3
  N46: relay_2.pin1, NO_/_NC_5.1
  N47: relay_2.pin2, NO_/_NC_5.3
  N48: relay_2.pin5, R26.Pin_1, ULN2003/4.Out_6
  N49: NO_/_NC_6.1, relay_1.pin1
  N50: NO_/_NC_6.3, relay_1.pin2
  N51: R21.Pin_1, LED15.anode
  N52: R22.Pin_0, LED16.cathode
  N53: LED17.cathode, R23.Pin_0
  N54: LED18.cathode, R24.Pin_0
  N55: LED19.cathode, R25.Pin_0
  N56: LED20.cathode, R26.Pin_0
  N57: LED21.cathode, R27.Pin_0
  N58: R27.Pin_1, ULN2003/4.Out_7, relay_1.pin5
  N59: S7.L2, R28.Pin_1
  N60: S9.L2, R29.Pin_1
  N61: S11.L2, R30.Pin_1
  N62: R28.Pin_0, LED22.cathode
  N63: LED23.cathode, R29.Pin_0
  N64: LED24.cathode, R30.Pin_0
  N65: LED25.cathode, R31.Pin_0
  N66: R31.Pin_1, S13.L2
  N67: LED26.cathode, R32.Pin_0
  N68: R32.Pin_1, S15.L2
  N69: LED27.cathode, R33.Pin_0
  N70: R33.Pin_1, S17.L2

notes:
  GND
  A1
  A2
  A3
  A4
  A5
  A0
  Rst
  5V
  Vin
  D2
  D3
  D4
  D5
  D6
  D7
  D11
  D10
  D8
  D12
  D13
  D9
  MIDI TOY CONTROLLER
  MIDI CH.11
  N.57
  (A3)
  N.48
  (C3)
  N.50
  (D3)
  N.52
  (E3)
  (F3)
  N.53
  (G3)
  N.55

custom parts:
  DIP - 8 pins: A DIP stand-in part for whatever IC you want. With 8 pins on a 300mil dual inline package (DIP) footprint.
  SPDT Toggle Switch: SPDT Toggle Switch. On-On

// code stored in the sketch: MIDI_Callbacks_Rocoto_Relays_Version_II.ino
#include <MIDI.h> //incluye librer�a MIDI
MIDI_CREATE_DEFAULT_INSTANCE();//�sto va siempre que uses la librer�a
int cantidad = 6;
int outPin[6] = {
  2 , 3 , 4 , 5 , 6, 7
} ; //defino los numeros de salida digital
int inPin[6] = {
  10 , 9 , 8 , 11 , 12, 13
}; //defino los numeros de entrada digital

int analogInput[6] = {
  A0, A1, A2, A3, A4, A5
};
int notas[6] = {
  48, 49, 50, 51, 52, 53
};//ac� definis las notas MIDI
//  54, 55, 56, 57, 58, 59};
//   60, 61, 62, 63, 63, 63};
int canalMIDI[6] = {
  11, 11, 11, 12, 12, 12
};
boolean estadoSalida [6] ;
boolean estadoPalanca[6];
unsigned long tiempoApagado [6];
int tiempoMin = 40; //tiempo minimo encendido
int tiempoMax = 10000; //tiempo maximo encendido (en milisegundos)


void activarPin(int i) {

  int valorPote = analogRead (analogInput[i]);
  int tiempoEncendido = map (valorPote, 0, 1023, tiempoMin, tiempoMax); // si quer�s, pod�s dejar un tiempo fijo ac� y listo
  estadoSalida[i] = true;
  tiempoApagado[i] = millis() + tiempoEncendido;
  digitalWrite(outPin[i], HIGH);
}


void HandleNoteOn(byte channel, byte pitch, byte velocity) {


      for (int i = 0; i < cantidad; i++) {
       estadoPalanca[i]= digitalRead (inPin[i]);
       if (estadoPalanca[i] == LOW) {
        if (channel == canalMIDI[i]) {
       
          if (pitch == notas[i]) {
            activarPin(i);
         }
        }
      }
      }  
}

void setup() {
  for (int i = 0 ; i < cantidad; i++) {
    estadoSalida[i] = 0;
    pinMode(outPin[i], OUTPUT);
    pinMode(inPin[i], INPUT_PULLUP);
  }
  MIDI.begin(MIDI_CHANNEL_OMNI);
  MIDI.setHandleNoteOn(HandleNoteOn);

}


void loop() {
  for (int i = 0 ; i < cantidad; i++) {
    if (estadoSalida[i]) {
      if (millis () > tiempoApagado[i]) {
        estadoSalida[i] = false;
        digitalWrite (outPin[i], LOW);
      }
    }
  }
  MIDI.read();

}
