# Fritzing sketch ULUPICA-MK2-not-tested (saved by Fritzing 0.9.3b)
circuit board: 9.2178cm x 4.70681cm
breadboards: 1

parts:
  OUT_1 = DIN-5 jack (MIDI) [package=THT]
  OUT_2 = DIN-5 jack (MIDI) [package=THT]
  OUT_3 = DIN-5 jack (MIDI) [package=THT]
  OUT_4 = DIN-5 jack (MIDI) [package=THT]
  R2 = Resistor [tolerance=±5% resistance=220 package=THT]
  1N4148 = Schottky Diode [part_number=1N4148 package="300 mil [THT]"]
  IN = DIN-5 jack (MIDI) [package=THT]
  6N138 = IC, DIP package, 8 pins [chip_label=IC]
  R1 = Resistor [tolerance=±5% resistance=220 package=THT]
  R5 = Resistor [tolerance=±5% resistance=220 package=THT]
  R3 = Resistor [tolerance=±5% resistance=220 package=THT]
  R6 = Resistor [tolerance=±5% resistance=220 package=THT]
  R8 = Resistor [tolerance=±5% resistance=220 package=THT]
  R7 = Resistor [tolerance=±5% resistance=220 package=THT]
  R4 = Resistor [tolerance=±5% resistance=220 package=THT]
  R9 = Resistor [tolerance=±5% resistance=220 package=THT]
  R12 = Resistor [tolerance=±5% resistance=220 package=THT]
  OUT_5 = DIN-5 jack (MIDI) [package=THT]
  R10 = Resistor [tolerance=±5% resistance=220 package=THT]
  R11 = Resistor [tolerance=±5% resistance=220 package=THT]
  LED = LED - 3mm [color="Red (633nm)" package="3 mm [THT]"]
  R13 = Resistor [tolerance=±5% resistance=470 package=THT]
  J3 = Generic female header - 1 pins [form="♀ (female)" package=THT]  # not connected
  74HC14 = SN74LS14N [package="DIP14 [THT]"]
  USB_(no_data_just_power) = USB connector [package=THT]

nets:
  N1: OUT_1.5, R5.Pin_0
  GND: OUT_1.2, OUT_2.2, OUT_3.2, OUT_4.2, 6N138.pin5, OUT_5.2, LED.cathode, 74HC14.GND, USB_(no_data_just_power).GND
  N2: OUT_1.4, R3.Pin_0
  N3: OUT_2.5, R6.Pin_0
  N4: OUT_2.4, R4.Pin_1
  N5: OUT_3.5, R8.Pin_0
  N6: OUT_3.4, R7.Pin_1
  N7: OUT_4.5, R9.Pin_0
  N8: OUT_4.4, R12.Pin_1
  VCC: R2.Pin_0, 6N138.pin8, R3.Pin_1, R7.Pin_0, R4.Pin_0, R12.Pin_0, R11.Pin_0, R13.Pin_1, 74HC14.VCC, USB_(no_data_just_power).5V
  N9: R2.Pin_1, 6N138.pin6, 74HC14.1A
  N10: 1N4148.cathode, 6N138.pin2, R1.Pin_1
  N11: 1N4148.anode, IN.5, 6N138.pin3
  N12: IN.4, R1.Pin_0
  N13: R5.Pin_1, 74HC14.2Y
  N14: R6.Pin_1, 74HC14.3Y
  N15: R8.Pin_1, 74HC14.6Y
  N16: R9.Pin_1, 74HC14.5Y
  N17: OUT_5.5, R10.Pin_0
  N18: OUT_5.4, R11.Pin_1
  N19: R10.Pin_1, 74HC14.4Y
  N20: LED.anode, R13.Pin_0
  N21: 74HC14.1Y, 74HC14.2A, 74HC14.3A, 74HC14.4A, 74HC14.5A, 74HC14.6A

notes:
  6N138
  MIDI THRU BOX, LABORATORIO DE JUGUETE
  MIDI
  Thru Box
  USB
  NO DATA
  JUST POWER

custom parts:
  Generic female header - 1 pins: Generic female header
