# Fritzing sketch ULUPICA (saved by Fritzing 0.9.3b)
circuit board: 9.2178cm x 4.70681cm
breadboards: 1

parts:
  OUT_1 = DIN-5 jack (MIDI) [package=THT]
  OUT_2 = DIN-5 jack (MIDI) [package=THT]
  OUT_3 = DIN-5 jack (MIDI) [package=THT]
  OUT_4 = DIN-5 jack (MIDI) [package=THT]
  R2 = Resistor [tolerance=±5% resistance=220 package=THT]
  1N4148 = Schottky Diode [part_number=1N4148 package="300 mil [THT]"]
  IN = DIN-5 jack (MIDI) [package=THT]
  6N138 = IC, DIP package, 8 pins [chip_label=IC]
  R1 = Resistor [tolerance=±5% resistance=220 package=THT]
  R5 = Resistor [tolerance=±5% resistance=220 package=THT]
  R3 = Resistor [tolerance=±5% resistance=220 package=THT]
  Power_plug2 = Power plug
  7805 = Voltage Regulator - 5V [package="TO220 [THT]"]
  10uF = Electrolytic Capacitor [capacitance=10µF package="100 mil [THT, electrolytic]"]
  1N4007 = Rectifier Diode [part_number=1N4001 package="300 mil [THT]"]
  R6 = Resistor [tolerance=±5% resistance=220 package=THT]
  R8 = Resistor [tolerance=±5% resistance=220 package=THT]
  R7 = Resistor [tolerance=±5% resistance=220 package=THT]
  R4 = Resistor [tolerance=±5% resistance=220 package=THT]
  R9 = Resistor [tolerance=±5% resistance=220 package=THT]
  R12 = Resistor [tolerance=±5% resistance=220 package=THT]
  OUT_5 = DIN-5 jack (MIDI) [package=THT]
  R10 = Resistor [tolerance=±5% resistance=220 package=THT]
  R11 = Resistor [tolerance=±5% resistance=220 package=THT]
  LED = LED - 3mm [color="Red (633nm)" package="3 mm [THT]"]
  R13 = Resistor [tolerance=±5% resistance=470 package=THT]
  0_1uF = Ceramic Capacitor [capacitance=100nF package="100 mil [THT, multilayer]"]
  J3 = Generic female header - 1 pins [form="♀ (female)" package=THT]  # not connected
  74HC14 = SN74LS14N [package="DIP14 [THT]"]

nets:
  N1: OUT_1.5, R5.Pin_0
  GND: OUT_1.2, OUT_2.2, OUT_3.2, OUT_4.2, 6N138.pin5, Power_plug2.GND, 7805.GND, 10uF.-, OUT_5.2, LED.cathode, 0_1uF.1, 74HC14.GND
  N2: OUT_1.4, R3.Pin_0
  N3: OUT_2.5, R6.Pin_0
  N4: OUT_2.4, R4.Pin_1
  N5: OUT_3.5, R8.Pin_0
  N6: OUT_3.4, R7.Pin_1
  N7: OUT_4.5, R9.Pin_0
  N8: OUT_4.4, R12.Pin_1
  N9: R2.Pin_0, 6N138.pin8, R3.Pin_1, 7805.output_voltage, R7.Pin_0, R4.Pin_0, R12.Pin_0, R11.Pin_0, R13.Pin_1, 0_1uF.0, 74HC14.VCC
  N10: R2.Pin_1, 6N138.pin6, 74HC14.1A
  N11: 1N4148.cathode, 6N138.pin2, R1.Pin_1
  N12: 1N4148.anode, IN.5, 6N138.pin3
  N13: IN.4, R1.Pin_0
  N14: R5.Pin_1, 74HC14.2Y
  N15: Power_plug2.VCC, 1N4007.anode
  N16: 7805.input_voltage, 10uF.+, 1N4007.cathode
  N17: R6.Pin_1, 74HC14.3Y
  N18: R8.Pin_1, 74HC14.6Y
  N19: R9.Pin_1, 74HC14.5Y
  N20: OUT_5.5, R10.Pin_0
  N21: OUT_5.4, R11.Pin_1
  N22: R10.Pin_1, 74HC14.4Y
  N23: LED.anode, R13.Pin_0
  N24: 74HC14.1Y, 74HC14.2A, 74HC14.3A, 74HC14.4A, 74HC14.5A, 74HC14.6A

notes:
  9/12V
  +•)-
  6N138
  MIDI THRU BOX, LABORATORIO DE JUGUETE
  MIDI
  Thru Box

custom parts:
  Generic female header - 1 pins: Generic female header
